# Fritzing sketch fritzing diagram (saved by Fritzing 0.9.6b)
breadboards: 1

parts:
  Part1 = RFID-RC522-v3
  Part2 = Arduino Nano (Rev3.0)
  HC-SR04_Sensor_1 = HC-SR04 Ultrasonic Distance Sensor
  KEYPAD1 = Membrane Matrix Keypad
  VCC1 = Battery block 9V
  U1 = RELAY [package=relay-jzc]
  M1 = DC Motor

nets:
  N1: Part1.SDA, Part2.D10
  N2: Part1.SCK, Part2.D13/SCK
  N3: Part1.MOSI, Part2.D11/MOSI
  N4: Part1.MISO, Part2.D12/MISO
  GND: Part1.GND, Part2.GND, HC-SR04_Sensor_1.GND, VCC1.-, U1.COIL2, M1.pin_1
  N5: Part1.RST, Part2.D9
  3.3V: Part1.3.3V, Part2.3V3
  N6: Part2.D2, KEYPAD1.7
  N7: Part2.D3, KEYPAD1.6
  N8: Part2.D4, KEYPAD1.5
  N9: Part2.D5, KEYPAD1.4
  N10: Part2.D6, KEYPAD1.3
  N11: Part2.D7, KEYPAD1.2
  N12: Part2.D8, KEYPAD1.1
  VIN: Part2.VIN, HC-SR04_Sensor_1.VCC, VCC1.+, U1.MAIN
  N13: Part2.A5, U1.COIL1
  N14: Part2.A3, HC-SR04_Sensor_1.ECHO
  N15: Part2.A2, HC-SR04_Sensor_1.TRIG
  N16: U1.NC, M1.pin_2

custom parts:
  RFID-RC522-v3: A simple China made RFID-RC522 Reader (6x4 cm); do check the pin labels, as this is a MFRC522 based clone.
  Membrane Matrix Keypad: Membrane Matrix 3x4 Keypad
